# Fritzing sketch Esquema (saved by Fritzing 0.9.3b)
breadboards: 1

parts:
  WeMos_D1_Mini_WS2812B_RGB_Shield1 = WeMos D1 Mini WS2812B RGB Shield
  R1 = Resistor [tolerance=±5% resistance=5 package="0402 [SMD]"]
  R2 = Resistor [tolerance=±5% resistance=5 package="0402 [SMD]"]
  HLK-PM1 = HLK-PM01
  LM1 = RioRand LM2596
  Part1 = 4N25 [package=THT]
  Part2 = 4N25 [package=THT]

nets:
  N1: WeMos_D1_Mini_WS2812B_RGB_Shield1.5V, LM1.Pin_2
  N2: WeMos_D1_Mini_WS2812B_RGB_Shield1.D1, Part2.Pin_1
  N3: WeMos_D1_Mini_WS2812B_RGB_Shield1.D2, Part1.Pin_1
  -COMANDO/GND: WeMos_D1_Mini_WS2812B_RGB_Shield1.G, R1.Pin_0, R2.Pin_0, HLK-PM1.-Vo, LM1.Pin_1, LM1.Pin_3
  N4: R1.Pin_1, Part1.Pin_2
  N5: R2.Pin_1, Part2.Pin_2
  +COMANDO: HLK-PM1.+Vo, LM1.Pin_0
  BPIN2_COMANDO: Part1.Pin_4
  BPIN1_COMANDO: Part1.Pin_5
  APIN2_COMANDO: Part2.Pin_4
  APIN1_COMANDO: Part2.Pin_5

custom parts:
  4N25: Optocoupler
